// Logisim project 8-Bit Simple ALU.circ as structural Verilog: 5 circuits, main circuit Main
module Main (
  input  [1:0] Op,
  input  [7:0] A,
  input  [7:0] B,
  output [7:0] R,
  output Co
);

  _8Bit_ALU u_8bit_alu_1 (.Op(Op), .A(A), .B(B), .R(R), .Co(Co));

  // Notes on the sheet:
  //   HW3 Simple 8 bit ALU
  //   학번 : 19011447
  //   이름 : 석민규
endmodule

module \전가산기  (
  input  a,
  input  b,
  input  ci,
  output s,
  output co
);

  wire and_1_out, and_2_out, xor_1_out;

  xor xor_1 (xor_1_out, a, b);
  and and_1 (and_1_out, b, a);
  xor xor_2 (s, xor_1_out, ci);
  and and_2 (and_2_out, ci, xor_1_out);
  or or_1 (co, and_2_out, and_1_out);
endmodule

module _1bit_ALU (
  input  a,
  input  b,
  input  ci,
  input  [1:0] Op,
  output out_5,
  output R
);

  wire and_1_out, or_1_out, xor_1_out, \전가산기_1_s ;

  and and_1 (and_1_out, b, a);
  or or_1 (or_1_out, b, a);
  xor xor_1 (xor_1_out, b, Op[0]);
  \전가산기  \u_전가산기_1  (.a(a), .b(xor_1_out), .ci(ci), .s(\전가산기_1_s ), .co(out_5));
  Multiplexer #(.select(2)) multiplexer_1 (
    .in0(\전가산기_1_s ), .in1(\전가산기_1_s ), .in2(and_1_out), .in3(or_1_out), .out(R), .sel(Op));  // open: en
endmodule

module _4bit_ALU (
  input  Ci,
  input  [1:0] Op,
  input  [3:0] A,
  input  [3:0] B,
  output [3:0] Result,
  output Co
);

  wire n1bit_alu_1_out_5, n1bit_alu_2_out_5, n1bit_alu_3_out_5;

  _1bit_ALU u_1bit_alu_1 (.a(A[0]), .b(B[0]), .ci(Ci), .out_5(n1bit_alu_1_out_5), .R(Result[0]), .Op(Op));
  _1bit_ALU u_1bit_alu_2 (
    .a(A[1]), .b(B[1]), .ci(n1bit_alu_1_out_5), .out_5(n1bit_alu_2_out_5), .R(Result[1]), .Op(Op));
  _1bit_ALU u_1bit_alu_3 (
    .a(A[2]), .b(B[2]), .ci(n1bit_alu_2_out_5), .out_5(n1bit_alu_3_out_5), .R(Result[2]), .Op(Op));
  _1bit_ALU u_1bit_alu_4 (.a(A[3]), .b(B[3]), .ci(n1bit_alu_3_out_5), .out_5(Co), .R(Result[3]), .Op(Op));
endmodule

module _8Bit_ALU (
  input  [1:0] Op,
  input  [7:0] A,
  input  [7:0] B,
  output [7:0] R,
  output Co
);

  wire n4bit_alu_1_co;

  _4bit_ALU u_4bit_alu_1 (.Ci(Op[0]), .A(A[3:0]), .B(B[3:0]), .Result(R[3:0]), .Co(n4bit_alu_1_co), .Op(Op));
  _4bit_ALU u_4bit_alu_2 (.Ci(n4bit_alu_1_co), .A(A[7:4]), .B(B[7:4]), .Result(R[7:4]), .Co(Co), .Op(Op));
endmodule
