// Logisim project Digital Clock.circ as structural Verilog: 7 circuits, main circuit main
module main (
);

  wire and_1_out, clock_1_out, mod_12_1_qh, mod_12_1_tc, mod_60_1_tc, mod_60_2_tc, nand_1_out;
  wire [2:0] mod_60_1_qh, mod_60_2_qh;
  wire [3:0] mod_12_1_ql, mod_60_1_ql, mod_60_2_ql;
  wire [6:0] apm_1_c0, apm_1_c1, apm_1_c2, apm_1_c3, apm_1_c4, apm_1_m0, apm_1_m1, apm_1_m2, apm_1_m3,
       apm_1_m4;

  apm apm_1 (
    .CK(clock_1_out), .ov_prime(nand_1_out), .C4(apm_1_c4), .C3(apm_1_c3), .C2(apm_1_c2), .C1(apm_1_c1),
    .C0(apm_1_c0), .M4(apm_1_m4), .M3(apm_1_m3), .M2(apm_1_m2), .M1(apm_1_m1), .M0(apm_1_m0));
  DotMatrix dotmatrix_1 (.col0(apm_1_c4), .col1(apm_1_c3), .col2(apm_1_c2), .col3(apm_1_c1), .col4(apm_1_c0));
  DotMatrix dotmatrix_2 (.col0(apm_1_m4), .col1(apm_1_m3), .col2(apm_1_m2), .col3(apm_1_m1), .col4(apm_1_m0));
  nand nand_1 (nand_1_out, mod_60_2_tc, mod_60_1_tc, mod_12_1_tc);
  _7_Segment_Display u_7_segment_display_1 (.d(mod_12_1_qh));  // open: g, f, a, b, e, c, dp
  and and_1 (and_1_out, mod_60_1_tc, mod_60_2_tc);
  Clock clock_1 (.out(clock_1_out));
  _7_Segment_Display u_7_segment_display_2 (.d(mod_60_1_qh[0]));  // open: g, f, a, b, e, c, dp
  Hex_Digit_Display hex_digit_display_1 (.value(mod_12_1_ql));  // open: dp
  mod_12 mod_12_1 (.en(and_1_out), .ck(clock_1_out), .TC(mod_12_1_tc), .QH(mod_12_1_qh), .QL(mod_12_1_ql));
  Hex_Digit_Display hex_digit_display_2 (.value(mod_60_1_ql));  // open: dp
  mod_60 mod_60_1 (.en(mod_60_2_tc), .ck(clock_1_out), .TC(mod_60_1_tc), .QH(mod_60_1_qh), .QL(mod_60_1_ql));
  _7_Segment_Display u_7_segment_display_3 (.d(mod_60_2_qh[0]));  // open: g, f, a, b, e, c, dp
  Hex_Digit_Display hex_digit_display_3 (.value(mod_60_2_ql));  // open: dp
  mod_60 mod_60_2 (.en(1'b1), .ck(clock_1_out), .TC(mod_60_2_tc), .QH(mod_60_2_qh), .QL(mod_60_2_ql));
  // Pins of 1 and 3 bits meet at mod_60_1_qh
  // Pins of 1 and 3 bits meet at mod_60_2_qh

  // Notes on the sheet:
  //   HW5 디지털시계
  //   시
  //   학번: 19011447
  //   이름: 석민규
  //   분
  //   초
endmodule

module apm (
  input  CK,
  input  ov_prime,
  output [6:0] C4,
  output [6:0] C3,
  output [6:0] C2,
  output [6:0] C1,
  output [6:0] C0,
  output [6:0] M4,
  output [6:0] M3,
  output [6:0] M2,
  output [6:0] M1,
  output [6:0] M0
);

  wire not_1_out;

  T_Flip_Flop t_ff_1 (.clk(CK), .T(not_1_out), .Q(C0[4]), .Qn(C0[2]));  // open: preset, reset, en
  not not_1 (not_1_out, ov_prime);
  DotMatrix dotmatrix_1 (
    .col0({1'b0, {2{C0[4]}}, 4'b1111}), .col1({1'b0, C0[4], C0[2], 4'b0100}), .col2(7'b0100100),
    .col3({1'b0, C0[4], C0[2], 4'b0100}), .col4({2'b00, C0[4], 1'b1, {3{C0[2]}}}));
  DotMatrix dotmatrix_2 (.col0(7'b0111111), .col1(7'b0010000), .col2(7'b0001000), .col3(7'b0010000), .col4(7'b0111111));

  assign {C0[6:5], C0[3], C0[1:0]} = {3'b001, {2{C0[2]}}};
  assign C1 = {1'b0, C0[4], C0[2], 4'b0100};
  assign C2 = 7'b0100100;
  assign C3 = {1'b0, C0[4], C0[2], 4'b0100};
  assign C4 = {1'b0, {2{C0[4]}}, 4'b1111};
  assign M0 = 7'b0111111;
  assign M1 = 7'b0010000;
  assign M2 = 7'b0001000;
  assign M3 = 7'b0010000;
  assign M4 = 7'b0111111;

  // Other names for the same wires on the sheet: A = C0[2]; AP0 (some bits) = {C0[4], {3{C0[2]}}};
  //   AP1[5:4] = {C0[4], C0[2]}; AP3[5:4] = {C0[4], C0[2]}; AP4[5:4] = {2{C0[4]}}; P = C0[4]
endmodule

module mod_10 (
  input  en,
  input  cir_prime,
  input  ck,
  output TC,
  output [3:0] Q
);

  wire and_1_out, and_2_out, and_3_out, and_4_out, and_5_out, and_6_out, and_7_out, multiplexer_1_out,
       multiplexer_2_out, multiplexer_3_out, multiplexer_4_out, not_2_out, not_3_out, not_4_out, not_5_out,
       not_6_out, not_7_out, not_8_out, not_9_out, not_10_out, or_1_out, or_2_out, or_3_out;
  wire [0:0] not_1_out;

  not not_1 (not_1_out[0], cir_prime);
  Multiplexer #(.select(2)) multiplexer_1 (
    .in1(1'b1), .out(multiplexer_1_out), .sel({1'b0, not_1_out[0]}), .en(en));  // open: in0, in2, in3
  not not_2 (not_2_out, Q[0]);
  D_Flip_Flop d_ff_1 (.clk(ck), .D(not_2_out), .Q(Q[0]));  // open: Qn, preset, en, reset
  Multiplexer #(.select(2)) multiplexer_2 (
    .in1(1'b0), .in2(1'b0), .out(multiplexer_2_out), .sel({1'b0, not_1_out[0]}), .en(en));  // open: in0, in3
  and and_1 (and_1_out, not_8_out, not_4_out, Q[0]);
  and and_2 (and_2_out, not_2_out, Q[1]);
  not not_3 (not_3_out, Q[0]);
  not not_4 (not_4_out, Q[1]);
  D_Flip_Flop d_ff_2 (.clk(ck), .D(or_1_out), .Q(Q[1]));  // open: Qn, preset, en, reset
  or or_1 (or_1_out, and_1_out, and_2_out);
  not not_5 (not_5_out, Q[1]);
  not not_6 (not_6_out, Q[1]);
  Multiplexer #(.select(2)) multiplexer_3 (
    .in1(1'b0), .out(multiplexer_3_out), .sel({1'b0, not_1_out[0]}), .en(en));  // open: in0, in2, in3
  not not_7 (not_7_out, Q[2]);
  and and_3 (and_3_out, not_7_out, Q[1], Q[0]);
  and and_4 (and_4_out, Q[2], not_5_out);
  and and_5 (and_5_out, Q[2], not_3_out);
  not not_8 (not_8_out, Q[3]);
  or or_2 (or_2_out, and_3_out, and_4_out, and_5_out);
  not not_9 (not_9_out, Q[2]);
  D_Flip_Flop d_ff_3 (.clk(ck), .D(or_2_out), .Q(Q[2]));  // open: Qn, preset, en, reset
  not not_10 (not_10_out, Q[0]);
  Multiplexer #(.select(2)) multiplexer_4 (
    .in1(1'b1), .out(multiplexer_4_out), .sel({1'b0, not_1_out[0]}), .en(en));  // open: in0, in2, in3
  and and_6 (and_6_out, Q[2], Q[1], Q[0]);
  and and_7 (and_7_out, Q[3], not_10_out);
  or or_3 (or_3_out, and_6_out, and_7_out);
  D_Flip_Flop d_ff_4 (.clk(ck), .D(or_3_out), .Q(Q[3]));  // open: Qn, preset, en, reset
  and and_8 (TC, Q[0], not_6_out, not_9_out, Q[3]);
endmodule

module mod_6 (
  input  ck,
  input  en,
  input  cir_prime,
  output TC,
  output [2:0] Q
);

  wire and_1_out, and_2_out, and_3_out, and_4_out, multiplexer_1_out, multiplexer_2_out, multiplexer_3_out,
       not_2_out, not_3_out, not_4_out, not_5_out, or_1_out, or_2_out;
  wire [0:0] not_1_out;

  not not_1 (not_1_out[0], cir_prime);
  Multiplexer #(.select(2)) multiplexer_1 (
    .out(multiplexer_1_out), .sel({1'b0, not_1_out[0]}), .en(en));  // open: in0, in1, in2, in3
  not not_2 (not_2_out, Q[0]);
  D_Flip_Flop d_ff_1 (.clk(ck), .D(not_2_out), .Q(Q[0]));  // open: Qn, preset, en, reset
  and and_1 (and_1_out, not_5_out, not_3_out, Q[0]);
  and and_2 (and_2_out, not_2_out, Q[1]);
  Multiplexer #(.select(2)) multiplexer_2 (
    .out(multiplexer_2_out), .sel({1'b0, not_1_out[0]}), .en(en));  // open: in0, in1, in2, in3
  or or_1 (or_1_out, and_1_out, and_2_out);
  not not_3 (not_3_out, Q[1]);
  D_Flip_Flop d_ff_2 (.clk(ck), .D(or_1_out), .Q(Q[1]));  // open: Qn, preset, en, reset
  not not_4 (not_4_out, Q[1]);
  and and_3 (and_3_out, Q[2], not_2_out);
  and and_4 (and_4_out, Q[1], Q[0]);
  Multiplexer #(.select(2)) multiplexer_3 (
    .out(multiplexer_3_out), .sel({1'b0, not_1_out[0]}), .en(en));  // open: in0, in1, in2, in3
  not not_5 (not_5_out, Q[2]);
  or or_2 (or_2_out, and_3_out, and_4_out);
  D_Flip_Flop d_ff_3 (.clk(ck), .D(or_2_out), .Q(Q[2]));  // open: Qn, preset, en, reset
  and and_5 (TC, Q[0], not_4_out, Q[2]);
endmodule

module mod_2 (
  input  en,
  input  cir_prime,
  input  ck,
  output Q,
  output TC
);

  wire multiplexer_1_out, not_2_out;
  wire [0:0] not_1_out;

  not not_1 (not_1_out[0], cir_prime);
  Multiplexer #(.select(2)) multiplexer_1 (
    .out(multiplexer_1_out), .sel({1'b0, not_1_out[0]}), .en(en));  // open: in0, in1, in2, in3
  not not_2 (not_2_out, Q);
  D_Flip_Flop d_ff_1 (.clk(ck), .D(not_2_out), .Q(Q));  // open: Qn, preset, en, reset
  and and_1 (TC, Q, 1'b1);
endmodule

module mod_60 (
  input  en,
  input  ck,
  output TC,
  output [2:0] QH,
  output [3:0] QL
);

  wire mod_6_1_tc, mod_10_1_tc;

  mod_6 mod_6_1 (.en(en), .cir_prime(1'b1), .ck(ck), .TC(mod_6_1_tc), .Q(QH));
  mod_10 mod_10_1 (.cir_prime(1'b1), .ck(ck), .TC(mod_10_1_tc), .Q(QL));  // open: en
  and and_1 (TC, mod_6_1_tc, mod_10_1_tc);
endmodule

module mod_12 (
  input  en,
  input  ck,
  output TC,
  output QH,
  output [3:0] QL
);

  wire mod_2_1_tc, mod_10_1_tc;

  mod_2 mod_2_1 (.en(en), .ck(ck), .TC(mod_2_1_tc), .Q(QH));  // open: cir_prime
  mod_10 mod_10_1 (.ck(ck), .TC(mod_10_1_tc), .Q(QL));  // open: en, cir_prime
  and and_1 (TC, mod_2_1_tc, mod_10_1_tc);
endmodule
