// Logisim project ALU&Register Bank.circ as structural Verilog: 3 circuits, main circuit main
module main (
  input  [1:0] Rs,
  input  [7:0] Extinp,
  input  [1:0] Rd,
  input  [1:0] Func
);

  wire clock_1_out;
  wire [3:0] reg_bank_1_rout, reg_bank_1_rout_2;
  wire [7:0] alu_1_out, reg_bank_1_aout;

  Clock clock_1 (.out(clock_1_out));
  Hex_Digit_Display hex_digit_display_1 (.value(reg_bank_1_rout));  // open: dp
  Hex_Digit_Display hex_digit_display_2 (.value(reg_bank_1_rout_2));  // open: dp
  Reg_Bank reg_bank_1 (
    .Rs(Rs), .Extin(Extinp), .Ck(clock_1_out), .Rd(Rd), .Din(alu_1_out),
    .Rout({reg_bank_1_rout_2, reg_bank_1_rout}), .Aout(reg_bank_1_aout));
  Hex_Digit_Display hex_digit_display_3 (.value(reg_bank_1_aout[7:4]));  // open: dp
  Hex_Digit_Display hex_digit_display_4 (.value(reg_bank_1_aout[3:0]));  // open: dp
  Hex_Digit_Display hex_digit_display_5 (.value(alu_1_out[7:4]));  // open: dp
  Alu alu_1 (.R({reg_bank_1_rout_2, reg_bank_1_rout}), .A(reg_bank_1_aout), .Func(Func), .Out(alu_1_out));
  Hex_Digit_Display hex_digit_display_6 (.value(alu_1_out[3:0]));  // open: dp

  // Notes on the sheet:
  //   Hw1 연산과 레지스터 제어
  //   학번 : 19011447
  //   이름 : 석민규
endmodule

module Reg_Bank (
  input  [7:0] Extin,
  input  [1:0] Rs,
  input  [1:0] Rd,
  input  [7:0] Din,
  input  Ck,
  output [7:0] Rout,
  output [7:0] Aout
);

  wire decoder_1_out0, decoder_1_out1, decoder_1_out2, decoder_1_out3;
  wire [7:0] B_q, C_q, D_q;

  Decoder #(.select(2), .disabled(0), .enable("false")) decoder_1 (
    .out0(decoder_1_out0), .out1(decoder_1_out1), .out2(decoder_1_out2), .out3(decoder_1_out3), .sel(Rd));
  Register A (.D(Din), .en(decoder_1_out0), .Q(Aout), .clk(Ck));  // open: clr
  Register B (.D(Din), .en(decoder_1_out1), .Q(B_q), .clk(Ck));  // open: clr
  Register C (.D(Din), .en(decoder_1_out2), .Q(C_q), .clk(Ck));  // open: clr
  Register D (.D(Din), .en(decoder_1_out3), .Q(D_q), .clk(Ck));  // open: clr
  Multiplexer #(.select(2), .width(8), .disabled(0), .enable("false")) multiplexer_1 (
    .in0(Extin), .in1(B_q), .in2(C_q), .in3(D_q), .out(Rout), .sel(Rs));
endmodule

module Alu (
  input  [7:0] R,
  input  [7:0] A,
  input  [1:0] Func,
  output [7:0] Out
);

  wire [7:0] adder_1_out;

  Adder adder_1 (.a(R), .b(A), .out(adder_1_out), .cin(1'b0));  // open: cout
  Multiplexer #(.select(2), .width(8), .disabled(0), .enable("false")) multiplexer_1 (
    .in0(adder_1_out), .in1(R), .in2({A[0], A[7:1]}), .in3({A[6:0], A[7]}), .out(Out), .sel(Func));
endmodule
