// Logisim project Microprogrammed CPU.circ as structural Verilog: 7 circuits, main circuit main
module main (
);

  wire arMux, cAC, ck, iAC, iDR, iPC, L, not_1_out, T, wAC, wAR, wDR, wMEM, wPC, Z;
  wire [1:0] BR, CD, drMux, input_logic_1_s1s0;
  wire [2:0] ALU;
  wire [6:0] adder_1_out, CAR, multiplexer_4_out, Next, SBR_q;
  wire [10:0] AR_data_out, multiplexer_1_out, n16_to_11_1_out_2, PC;
  wire [15:0] AC, alu_1_aluout, DR, multiplexer_3_out, n11_to_16_1_out_2, ram_1_data;
  wire [27:26] rom_1_data;

  _16_to_11 u_16_to_11_1 (.in_1(DR), .out_2(n16_to_11_1_out_2));
  Hex_Digit_Display hex_digit_display_1 (.value({1'b0, PC[10:8]}));  // open: dp
  Multiplexer #(.width(11)) multiplexer_1 (
    .in0(n16_to_11_1_out_2), .in1(PC), .out(multiplexer_1_out), .sel(arMux));  // open: en
  Clock clock_1 (.out(ck));
  Hex_Digit_Display hex_digit_display_2 (.value(PC[7:4]));  // open: dp
  Hex_Digit_Display hex_digit_display_3 (.value(PC[3:0]));  // open: dp
  nor nor_1 (Z, AC[15], AC[14], AC[13], AC[12], AC[11], AC[10], AC[9], AC[8], AC[7], AC[6], AC[5], AC[4], AC[3], AC[2], AC[1], AC[0]);
  _11bit_register AR (
    .Data_IN(multiplexer_1_out), .Inc(1'b0), .Load(wAR), .Clock(ck), .Clear(1'b0), .Data_OUT(AR_data_out));
  Hex_Digit_Display hex_digit_display_4 (.value(AC[15:12]));  // open: dp
  not not_1 (not_1_out, wMEM);
  Hex_Digit_Display hex_digit_display_5 (.value(AC[11:8]));  // open: dp
  Hex_Digit_Display hex_digit_display_6 (.value(AC[7:4]));  // open: dp
  RAM #(.addrWidth(11), .dataWidth(16), .bus("separate")) ram_1 (
    .addr(AR_data_out), .din(DR), .data(ram_1_data), .str(wMEM), .clk(ck), .ld(not_1_out));  // open: sel, clr
  _11bit_register u_PC (.Data_IN(AR_data_out), .Inc(iPC), .Load(wPC), .Clock(ck), .Clear(1'b0), .Data_OUT(PC));
  _11_to_16 u_11_to_16_1 (.in_1(PC), .out_2(n11_to_16_1_out_2));
  Hex_Digit_Display hex_digit_display_7 (.value(AC[3:0]));  // open: dp
  Input_Logic input_logic_1 (.BR(BR), .T(T), .S1S0(input_logic_1_s1s0), .L(L));
  Multiplexer #(.select(2)) multiplexer_2 (
    .in0(1'b1), .in1(DR[15]), .in2(AC[15]), .in3(Z), .out(T), .sel(CD));  // open: en
  Multiplexer #(.select(2), .width(16)) multiplexer_3 (
    .in0(ram_1_data), .in1(AC), .in2(n11_to_16_1_out_2), .out(multiplexer_3_out), .sel(drMux));  // open: in3, en
  Hex_Digit_Display hex_digit_display_8 (.value(DR[15:12]));  // open: dp
  Hex_Digit_Display hex_digit_display_9 (.value(DR[11:8]));  // open: dp
  Hex_Digit_Display hex_digit_display_10 (.value(DR[7:4]));  // open: dp
  Hex_Digit_Display hex_digit_display_11 (.value(DR[3:0]));  // open: dp
  Multiplexer #(.select(2), .width(7)) multiplexer_4 (
    .in0(adder_1_out), .in1(Next), .in2(SBR_q), .in3({1'b1, DR[14:11], 2'b00}), .out(multiplexer_4_out),
    .sel(input_logic_1_s1s0));  // open: en
  Register #(.width(7)) u_CAR (.D(multiplexer_4_out), .Q(CAR), .clk(ck));  // open: en, clr
  _16_bit_register u_DR (.Data_IN(multiplexer_3_out), .Inc(iDR), .Load(wDR), .Clock(ck), .Clear(1'b0), .Data_OUT(DR));
  Adder #(.width(7)) adder_1 (.a(7'b0000001), .b(CAR), .out(adder_1_out));  // open: cin, cout
  ALU alu_1 (.func(ALU), .DR(DR), .AC(AC), .ALUout(alu_1_aluout));
  Hex_Digit_Display hex_digit_display_12 (.value({1'b0, CAR[6:4]}));  // open: dp
  Register #(.width(7)) SBR (.D(adder_1_out), .en(L), .Q(SBR_q), .clk(ck));  // open: clr
  _16_bit_register u_AC (.Data_IN(alu_1_aluout), .Inc(iAC), .Load(wAC), .Clock(ck), .Clear(cAC), .Data_OUT(AC));
  Hex_Digit_Display hex_digit_display_13 (.value(CAR[3:0]));  // open: dp
  ROM #(.addrWidth(7), .dataWidth(28)) rom_1 (
    .addr(CAR),
    .data({rom_1_data, wMEM, cAC, iAC, iDR, iPC, wAC, wDR, wPC, wAR, ALU, drMux, arMux, CD, BR, Next}));  // open: sel

  // Other names for the same wires on the sheet: Opcode[3:0] = DR[14:11]; S = AC[15]; I = DR[15]

  // Notes on the sheet:
  //   ALU
  //   HW4 Microprogrammed CPU
  //   학번 19011447
  //   이름 석민규
  //   Control Memory
  //   contents of rom_1 (hex, n*v repeats v):
  //   20801 280002 20180 80004 20100 59*0 283 80042 104000 0 446 0 283 40000 283 8104a 2000000 0 283 8004e
  //   18104f 2000000 40*0 78
endmodule

module _11bit_register (
  input  [10:0] Data_IN,
  input  Inc,
  input  Load,
  input  Clock,
  input  Clear,
  output [10:0] Data_OUT
);

  Counter #(.width(11), .max('h7ff)) counter_1 (
    .load(Load), .D(Data_IN), .count(Inc), .Q(Data_OUT), .clk(Clock), .clr(Clear));  // open: carry
endmodule

module _16_bit_register (
  input  [15:0] Data_IN,
  input  Inc,
  input  Load,
  input  Clock,
  input  Clear,
  output [15:0] Data_OUT
);

  Counter #(.width(16), .max('hffff)) counter_1 (
    .load(Load), .D(Data_IN), .count(Inc), .Q(Data_OUT), .clk(Clock), .clr(Clear));  // open: carry
endmodule

module _11_to_16 (
  input  [10:0] in_1,
  output [15:0] out_2
);


  assign out_2 = {{5{1'b0}}, in_1};
endmodule

module _16_to_11 (
  input  [15:0] in_1,
  output [10:0] out_2
);


  assign out_2 = in_1[10:0];
endmodule

module ALU (
  input  [2:0] func,
  input  [15:0] DR,
  input  [15:0] AC,
  output [15:0] ALUout
);

  wire [15:0] adder_1_out, and_1_out, not_1_out, or_1_out, subtractor_1_out, xor_1_out;

  Adder #(.width(16)) adder_1 (.a(AC), .b(DR), .out(adder_1_out));  // open: cin, cout
  Subtractor #(.width(16)) subtractor_1 (.a(AC), .b(DR), .out(subtractor_1_out));  // open: bin, bout
  assign or_1_out = AC | DR;  // OR_Gate or_1, 16 bits wide
  assign and_1_out = AC & DR;  // AND_Gate and_1, 16 bits wide
  assign xor_1_out = AC ^ DR;  // XOR_Gate xor_1, 16 bits wide
  assign not_1_out = ~AC;  // NOT_Gate not_1, 16 bits wide
  Multiplexer #(.select(3), .width(16)) multiplexer_1 (
    .in0(DR), .in1(adder_1_out), .in2(subtractor_1_out), .in3(or_1_out), .in4(and_1_out), .in5(xor_1_out),
    .in6(not_1_out), .out(ALUout), .sel(func));  // open: in7, en
endmodule

module Input_Logic (
  input  [1:0] BR,
  input  T,
  output [1:0] S1S0,
  output L
);

  wire and_1_out, and_2_out, not_1_out, not_2_out;

  not not_1 (not_1_out, BR[1]);
  not not_2 (not_2_out, BR[1]);
  and and_1 (and_1_out, BR[0], BR[1]);
  and and_2 (and_2_out, not_1_out, T);
  and and_3 (L, not_2_out, BR[0], T);
  or or_1 (S1S0[0], and_1_out, and_2_out);

  assign S1S0[1] = BR[1];
endmodule
