// Logisim project Mano CPU.circ as structural Verilog: 8 circuits, main circuit main
module main (
  input  [15:0] IR,
  output [6:0] InstMap
);

  wire ACP, ACZ, alu_1_co, and_1_out, cAC, cE, cIR, ck, cmE, DRZ, EZ, iAC, iAR, iDR, iIR, iPC, L, not_2_out,
       T, wAC, wAR, wDR, wE, wIR, wMEM, wPC;
  wire [1:0] BR, input_logic_1_s1s0;
  wire [2:0] ALUfunc, CD, S;
  wire [3:0] priority_encoder_1_out;
  wire [6:0] adder_1_out, CAR, InstMap_t, multiplexer_2_out, Next, SBR_q;
  wire [10:0] AR_data_out, n16_to_11_1_out_2, n16_to_11_2_out_2, PC_data_out;
  wire [15:0] AC, alu_1_aluout, DR, IR_t, multiplexer_3_out, n11_to_16_1_out_2, n11_to_16_2_out_2, ram_1_data;

  not not_1 (ACP, AC[15]);
  ALU alu_1 (.func(ALUfunc), .AC(AC), .DR(DR), .Ci(EZ), .ALUout(alu_1_aluout), .Co(alu_1_co));
  Input_Logic input_logic_1 (.BR(BR), .T(T), .S1S0(input_logic_1_s1s0), .L(L));
  Multiplexer #(.select(3)) multiplexer_1 (
    .in0(1'b1), .in1(DRZ), .in2(AC[15]), .in3(ACP), .in4(ACZ), .in5(EZ), .in6(IR[15]), .out(T), .sel(CD));  // open: in7, en
  Carry carry_1 (.E_IN(alu_1_co), .Comp(cmE), .load(wE), .E_OUT(EZ), .Clock(ck), .Clear(cE));
  nor nor_1 (DRZ, DR[15], DR[14], DR[13], DR[12], DR[11], DR[10], DR[9], DR[8], DR[7], DR[6], DR[5], DR[4], DR[3], DR[2], DR[1], DR[0]);
  nor nor_2 (ACZ, AC[15], AC[14], AC[13], AC[12], AC[11], AC[10], AC[9], AC[8], AC[7], AC[6], AC[5], AC[4], AC[3], AC[2], AC[1], AC[0]);
  _16_to_11 u_16_to_11_1 (.in_1(multiplexer_3_out), .out_2(n16_to_11_1_out_2));
  _16_to_11 u_16_to_11_2 (.in_1(multiplexer_3_out), .out_2(n16_to_11_2_out_2));
  Multiplexer #(.select(2), .width(7)) multiplexer_2 (
    .in0(adder_1_out), .in1(Next), .in2(SBR_q), .in3(InstMap_t), .out(multiplexer_2_out),
    .sel(input_logic_1_s1s0));  // open: en
  Register #(.width(7)) u_CAR (.D(multiplexer_2_out), .Q(CAR), .clk(ck));  // open: en, clr
  not not_2 (not_2_out, wMEM);
  Adder #(.width(7)) adder_1 (.a(7'b0000001), .b(CAR), .out(adder_1_out));  // open: cin, cout
  RAM #(.addrWidth(11), .dataWidth(16), .bus("separate")) ram_1 (
    .addr(AR_data_out), .din(multiplexer_3_out), .data(ram_1_data), .str(wMEM), .clk(ck), .ld(not_2_out));  // open: sel, clr
  _11bit_Register AR (
    .Data_IN(n16_to_11_1_out_2), .Inc(iAR), .Load(wAR), .Clock(ck), .Clear(1'b0), .Data_OUT(AR_data_out));
  _11bit_Register PC (
    .Data_IN(n16_to_11_2_out_2), .Inc(iPC), .Load(wPC), .Clock(ck), .Clear(1'b0), .Data_OUT(PC_data_out));
  _16bit_Register u_DR (.Data_IN(multiplexer_3_out), .Inc(iDR), .Load(wDR), .Clock(ck), .Clear(1'b0), .Data_OUT(DR));
  _16bit_Register u_AC (.Data_IN(alu_1_aluout), .Inc(iAC), .Load(wAC), .Clock(ck), .Clear(cAC), .Data_OUT(AC));
  _16bit_Register u_IR (.Data_IN(multiplexer_3_out), .Inc(iIR), .Load(wIR), .Clock(ck), .Clear(cIR), .Data_OUT(IR_t));
  and and_1 (and_1_out, IR[15], IR[14], IR[13], IR[12]);
  Register #(.width(7)) SBR (.D(adder_1_out), .en(L), .Q(SBR_q), .clk(ck));  // open: clr
  ROM #(.addrWidth(7), .dataWidth(32)) rom_1 (
    .addr(CAR),
    .data({wMEM, cmE, cE, cAC, iAC, iDR, iPC, iAR, wE, wIR, wAC, wDR, wPC, wAR, ALUfunc, S, CD, BR, Next}));  // open: sel
  _11_to_16 u_11_to_16_1 (.in_1(AR_data_out), .out_2(n11_to_16_1_out_2));
  _11_to_16 u_11_to_16_2 (.in_1(PC_data_out), .out_2(n11_to_16_2_out_2));
  Clock clock_1 (.out(ck));
  Multiplexer #(.select(3), .width(16)) multiplexer_3 (
    .in1(n11_to_16_1_out_2), .in2(n11_to_16_2_out_2), .in3(DR), .in4(AC), .in5(IR_t), .in7(ram_1_data),
    .out(multiplexer_3_out), .sel(S));  // open: in0, in6, en
  Priority_Encoder #(.select(4)) priority_encoder_1 (
    .in0(IR[10]), .in1(IR[9]), .in2(IR[8]), .in3(IR[7]), .in4(IR[6]), .in5(IR[5]), .in6(IR[4]), .in7(IR[3]),
    .in8(IR[2]), .in9(IR[1]), .in10(IR[0]), .in11(IR[11]), .out(priority_encoder_1_out), .en_in(and_1_out));  // open: in12, in13, in14, in15, gs, en_out
  Multiplexer #(.width(7)) multiplexer_4 (
    .in0({2'b01, IR[15:12], 1'b0}), .in1({2'b10, priority_encoder_1_out, 1'b0}), .out(InstMap),
    .sel(and_1_out));  // open: en

  // Other names for the same wires on the sheet: I = IR[15]; ACN = AC[15]

  // Notes on the sheet:
  //   Hw5 Mano CPU 구현
  //   학번: 19011447
  //   이름: 석민규
  //   Control Memory
  //   contents of rom_1 (hex, n*v repeats v):
  //   20801 280002 20180 80004 20100 59*0 283 80042 104000 0 446 0 283 40000 283 8104a 2000000 0 283 8004e
  //   18104f 2000000
endmodule

module _16bit_Register (
  input  [15:0] Data_IN,
  input  Inc,
  input  Load,
  input  Clock,
  input  Clear,
  output [15:0] Data_OUT
);

  Counter #(.width(16), .max('hffff)) counter_1 (
    .load(Load), .D(Data_IN), .count(Inc), .Q(Data_OUT), .clk(Clock), .clr(Clear));  // open: carry
endmodule

module _11bit_Register (
  input  [10:0] Data_IN,
  input  Inc,
  input  Load,
  input  Clock,
  input  Clear,
  output [10:0] Data_OUT
);

  Counter #(.width(11), .max('h7ff)) counter_1 (
    .load(Load), .D(Data_IN), .count(Inc), .Q(Data_OUT), .clk(Clock), .clr(Clear));  // open: carry
endmodule

module _16_to_11 (
  input  [15:0] in_1,
  output [10:0] out_2
);


  assign out_2 = in_1[10:0];
endmodule

module _11_to_16 (
  input  [10:0] in_1,
  output [15:0] out_2
);


  assign out_2 = {{5{1'b0}}, in_1};
endmodule

module ALU (
  input  [2:0] func,
  input  [15:0] AC,
  input  [15:0] DR,
  input  Ci,
  output [15:0] ALUout,
  output Co
);

  wire and_1_out, and_2_out, and_4_out, cout;
  wire [15:0] adder_1_out, and_3_out, not_1_out, not_2_out, xor_1_out;

  and and_1 (and_1_out, ~func[2], ~func[1], func[0], cout);  // AND_Gate
  and and_2 (and_2_out, func[2], ~func[1], ~func[0], AC[0]);  // AND_Gate
  assign and_3_out = AC & DR;  // AND_Gate and_3, 16 bits wide
  assign xor_1_out = DR ^ AC;  // XOR_Gate xor_1, 16 bits wide
  and and_4 (and_4_out, func[2], ~func[1], func[0], AC[15]);  // AND_Gate
  Adder #(.width(16)) adder_1 (.a(AC), .b(DR), .out(adder_1_out), .cout(cout));  // open: cin
  assign not_1_out = ~AC;  // NOT_Gate not_1, 16 bits wide
  assign not_2_out = ~DR;  // NOT_Gate not_2, 16 bits wide
  or or_1 (Co, and_4_out, and_2_out, and_1_out);
  Multiplexer #(.select(3), .width(16)) multiplexer_1 (
    .in0(and_3_out), .in1(adder_1_out), .in2(not_1_out), .in3(not_2_out), .in4({Ci, AC[15:1]}),
    .in5({AC[14:0], Ci}), .in6(xor_1_out), .in7(DR), .out(ALUout), .sel(func));  // open: en

  // Other names for the same wires on the sheet: b15 = AC[15]; b0 = AC[0]
endmodule

module Carry (
  input  E_IN,
  input  Comp,
  input  load,
  input  Clock,
  input  Clear,
  output E_OUT
);

  wire multiplexer_1_out, not_1_out;

  not not_1 (not_1_out, E_OUT);
  Multiplexer multiplexer_1 (.in0(E_IN), .in1(not_1_out), .out(multiplexer_1_out), .sel(Comp));  // open: en
  D_Flip_Flop d_ff_1 (.clk(Clock), .D(multiplexer_1_out), .Q(E_OUT), .en(load), .reset(Clear));  // open: Qn, preset
endmodule

module Input_Logic (
  input  [1:0] BR,
  input  T,
  output [1:0] S1S0,
  output L
);

  wire and_1_out, and_2_out, not_1_out, not_2_out;

  not not_1 (not_1_out, BR[1]);
  not not_2 (not_2_out, BR[1]);
  and and_1 (and_1_out, BR[0], BR[1]);
  and and_2 (and_2_out, not_1_out, T);
  and and_3 (L, not_2_out, BR[0], T);
  or or_1 (S1S0[0], and_1_out, and_2_out);

  assign S1S0[1] = BR[1];
endmodule
